// Logisim project Assignment1-StopWatchComplete.circ as structural Verilog: 8 circuits, main circuit main
module main (
);

  wire button_1_out, button_2_out, button_3_out, stage1_1_outstream;
  wire [3:0] stage4_1_minuteone, stage4_1_minuteten, stage4_1_secondone, stage4_1_secondten,
       stage6b_1_minuteoneout, stage6b_1_minutetenout, stage6b_1_secondoneout, stage6b_1_secondtenout,
       stage6b_2_minuteoneout, stage6b_2_minutetenout, stage6b_2_secondoneout, stage6b_2_secondtenout,
       stage6b_3_minuteoneout, stage6b_3_minutetenout, stage6b_3_secondoneout, stage6b_3_secondtenout,
       stage6b_4_minuteoneout, stage6b_4_minutetenout, stage6b_4_secondoneout, stage6b_4_secondtenout,
       stage6b_5_minuteoneout, stage6b_5_minutetenout, stage6b_5_secondoneout, stage6b_5_secondtenout;

  Button button_1 (.out(button_1_out));
  stage4 stage4_1 (
    .OnOffButton(stage1_1_outstream), .ResetButton(button_3_out), .SecondOne(stage4_1_secondone),
    .SecondTen(stage4_1_secondten), .MinuteTen(stage4_1_minuteten), .MinuteOne(stage4_1_minuteone));
  Button button_2 (.out(button_2_out));
  Hex_Digit_Display hex_digit_display_1 (.value(stage4_1_minuteten));  // open: dp
  Hex_Digit_Display hex_digit_display_2 (.value(stage4_1_minuteone));  // open: dp
  Button button_3 (.out(button_3_out));
  Hex_Digit_Display hex_digit_display_3 (.value(stage4_1_secondten));  // open: dp
  stage1 stage1_1 (.OnOff(button_1_out), .OutStream(stage1_1_outstream));
  Hex_Digit_Display hex_digit_display_4 (.value(stage4_1_secondone));  // open: dp
  LED led_1 (.in(stage1_1_outstream));
  Hex_Digit_Display hex_digit_display_5 (.value(stage6b_1_minutetenout));  // open: dp
  Hex_Digit_Display hex_digit_display_6 (.value(stage6b_1_minuteoneout));  // open: dp
  Hex_Digit_Display hex_digit_display_7 (.value(stage6b_2_minuteoneout));  // open: dp
  Hex_Digit_Display hex_digit_display_8 (.value(stage6b_2_minutetenout));  // open: dp
  Hex_Digit_Display hex_digit_display_9 (.value(stage6b_3_minuteoneout));  // open: dp
  Hex_Digit_Display hex_digit_display_10 (.value(stage6b_3_minutetenout));  // open: dp
  Hex_Digit_Display hex_digit_display_11 (.value(stage6b_1_secondtenout));  // open: dp
  Hex_Digit_Display hex_digit_display_12 (.value(stage6b_1_secondoneout));  // open: dp
  Hex_Digit_Display hex_digit_display_13 (.value(stage6b_2_secondtenout));  // open: dp
  Hex_Digit_Display hex_digit_display_14 (.value(stage6b_3_secondtenout));  // open: dp
  stage6b stage6b_1 (
    .SecondOne(stage4_1_secondone), .SecondTen(stage4_1_secondten), .MinuteOne(stage4_1_minuteone),
    .MinuteTen(stage4_1_minuteten), .Split(button_2_out), .Reset(button_3_out),
    .SecondOneOut(stage6b_1_secondoneout), .SecondTenOut(stage6b_1_secondtenout),
    .MinuteOneOut(stage6b_1_minuteoneout), .MinuteTenOut(stage6b_1_minutetenout));
  Hex_Digit_Display hex_digit_display_15 (.value(stage6b_2_secondoneout));  // open: dp
  stage6b stage6b_2 (
    .SecondOne(stage6b_1_secondoneout), .SecondTen(stage6b_1_secondtenout),
    .MinuteOne(stage6b_1_minuteoneout), .MinuteTen(stage6b_1_minutetenout), .Split(button_2_out),
    .Reset(button_3_out), .SecondOneOut(stage6b_2_secondoneout), .SecondTenOut(stage6b_2_secondtenout),
    .MinuteOneOut(stage6b_2_minuteoneout), .MinuteTenOut(stage6b_2_minutetenout));
  Hex_Digit_Display hex_digit_display_16 (.value(stage6b_3_secondoneout));  // open: dp
  stage6b stage6b_3 (
    .SecondOne(stage6b_2_secondoneout), .SecondTen(stage6b_2_secondtenout),
    .MinuteOne(stage6b_2_minuteoneout), .MinuteTen(stage6b_2_minutetenout), .Split(button_2_out),
    .Reset(button_3_out), .SecondOneOut(stage6b_3_secondoneout), .SecondTenOut(stage6b_3_secondtenout),
    .MinuteOneOut(stage6b_3_minuteoneout), .MinuteTenOut(stage6b_3_minutetenout));
  Hex_Digit_Display hex_digit_display_17 (.value(stage6b_4_minutetenout));  // open: dp
  Hex_Digit_Display hex_digit_display_18 (.value(stage6b_4_minuteoneout));  // open: dp
  Hex_Digit_Display hex_digit_display_19 (.value(stage6b_5_minutetenout));  // open: dp
  Hex_Digit_Display hex_digit_display_20 (.value(stage6b_4_secondtenout));  // open: dp
  Hex_Digit_Display hex_digit_display_21 (.value(stage6b_5_minuteoneout));  // open: dp
  Hex_Digit_Display hex_digit_display_22 (.value(stage6b_4_secondoneout));  // open: dp
  stage6b stage6b_4 (
    .SecondOne(stage6b_3_secondoneout), .SecondTen(stage6b_3_secondtenout),
    .MinuteOne(stage6b_3_minuteoneout), .MinuteTen(stage6b_3_minutetenout), .Split(button_2_out),
    .Reset(button_3_out), .SecondOneOut(stage6b_4_secondoneout), .SecondTenOut(stage6b_4_secondtenout),
    .MinuteOneOut(stage6b_4_minuteoneout), .MinuteTenOut(stage6b_4_minutetenout));
  Hex_Digit_Display hex_digit_display_23 (.value(stage6b_5_secondtenout));  // open: dp
  Hex_Digit_Display hex_digit_display_24 (.value(stage6b_5_secondoneout));  // open: dp
  stage6b stage6b_5 (
    .SecondOne(stage6b_4_secondoneout), .SecondTen(stage6b_4_secondtenout),
    .MinuteOne(stage6b_4_minuteoneout), .MinuteTen(stage6b_4_minutetenout), .Split(button_2_out),
    .Reset(button_3_out), .SecondOneOut(stage6b_5_secondoneout), .SecondTenOut(stage6b_5_secondtenout),
    .MinuteOneOut(stage6b_5_minuteoneout), .MinuteTenOut(stage6b_5_minutetenout));

  // Notes on the sheet:
  //   Start / Stop
  //   Stopwatch Interface
  //   Split
  //   Minutes
  //   Reset
  //   Elapsed Time
  //   Seconds
  //   :
  //   Clock Started
  //   Split Time 1
  //   Minutes
  //   :
  //   Minutes
  //   Minutes
  //   Seconds
  //   Split Time 2
  //   Seconds
  //   :
  //   Split Time 3
  //   Seconds
  //   :
  //   Minutes
  //   Split Time 4
  //   :
  //   Split Time 5
  //   Minutes
  //   :
  //   Seconds
  //   Seconds
endmodule

module stage1 (
  input  OnOff,
  output OutStream
);

  T_Flip_Flop t_ff_1 (.T(1'b1), .clk(OnOff), .Q(OutStream));  // open: Qn, reset, preset
endmodule

module stage2 (
  input  OnOffButton,
  input  ResetButton,
  output SO1,
  output SO2,
  output SO3,
  output SO4,
  output ResetMain,
  output ResetNext,
  output CLK
);

  wire and_1_out, and_3_out, and_4_out, or_1_out, t_ff_1_q, t_ff_2_q, t_ff_3_q, t_ff_4_q;

  Clock clock_1 (.out(CLK));
  T_Flip_Flop t_ff_1 (.T(OnOffButton), .clk(CLK), .Q(t_ff_1_q), .reset(or_1_out));  // open: Qn, preset
  D_Flip_Flop d_ff_1 (.D(t_ff_1_q), .clk(CLK), .Q(SO1));  // open: Qn, preset, reset
  T_Flip_Flop t_ff_2 (.T(t_ff_1_q), .clk(CLK), .Q(t_ff_2_q), .reset(or_1_out));  // open: Qn, preset
  D_Flip_Flop d_ff_2 (.D(t_ff_2_q), .clk(CLK), .Q(SO2));  // open: Qn, preset, reset
  and and_1 (and_1_out, t_ff_1_q, t_ff_2_q);
  T_Flip_Flop t_ff_3 (.T(and_1_out), .clk(CLK), .Q(t_ff_3_q), .reset(or_1_out));  // open: Qn, preset
  D_Flip_Flop d_ff_3 (.D(t_ff_3_q), .clk(CLK), .Q(SO3));  // open: Qn, preset, reset
  and and_2 (ResetNext, SO1, SO4);
  and and_3 (and_3_out, and_1_out, t_ff_3_q);
  T_Flip_Flop t_ff_4 (.T(and_3_out), .clk(CLK), .Q(t_ff_4_q), .reset(or_1_out));  // open: Qn, preset
  D_Flip_Flop d_ff_4 (.D(t_ff_4_q), .clk(CLK), .Q(SO4));  // open: Qn, preset, reset
  and and_4 (and_4_out, t_ff_2_q, t_ff_4_q);
  or or_1 (or_1_out, and_4_out, ResetButton);
  Hex_Digit_Display hex_digit_display_1 (.value({SO4, SO3, SO2, SO1}));  // open: dp

  assign ResetMain = ResetButton;
endmodule

module stage3 (
  input  OnOffButton,
  input  ResetButton,
  output ST1,
  output ST2,
  output ST3,
  output SO1,
  output SO2,
  output SO3,
  output SO4,
  output ResetNext,
  output CLK,
  output ResetMain
);

  wire and_1_out, and_2_out, stage2_1_resetnext, t_ff_1_q, t_ff_2_q, t_ff_3_q;

  T_Flip_Flop t_ff_1 (.T(1'b1), .clk(stage2_1_resetnext), .Q(t_ff_1_q), .reset(ResetNext));  // open: Qn, preset
  D_Flip_Flop d_ff_1 (.D(t_ff_1_q), .clk(CLK), .Q(ST1));  // open: Qn, preset, reset
  T_Flip_Flop t_ff_2 (.T(t_ff_1_q), .clk(stage2_1_resetnext), .Q(t_ff_2_q), .reset(ResetNext));  // open: Qn, preset
  D_Flip_Flop d_ff_2 (.D(t_ff_2_q), .clk(CLK), .Q(ST2));  // open: Qn, preset, reset
  and and_1 (and_1_out, t_ff_1_q, t_ff_2_q);
  T_Flip_Flop t_ff_3 (.T(and_1_out), .clk(stage2_1_resetnext), .Q(t_ff_3_q), .reset(ResetNext));  // open: Qn, preset
  D_Flip_Flop d_ff_3 (.D(t_ff_3_q), .clk(CLK), .Q(ST3));  // open: Qn, preset, reset
  and and_2 (and_2_out, t_ff_2_q, t_ff_3_q);
  stage2 stage2_1 (
    .OnOffButton(OnOffButton), .ResetButton(ResetButton), .SO1(SO1), .SO2(SO2), .SO3(SO3), .SO4(SO4),
    .ResetMain(ResetMain), .ResetNext(stage2_1_resetnext), .CLK(CLK));
  Hex_Digit_Display hex_digit_display_1 (.value({1'b0, ST3, ST2, ST1}));  // open: dp
  Hex_Digit_Display hex_digit_display_2 (.value({SO4, SO3, SO2, SO1}));  // open: dp
  or or_1 (ResetNext, and_2_out, ResetMain);
endmodule

module stage4 (
  input  OnOffButton,
  input  ResetButton,
  output [3:0] SecondOne,
  output [3:0] SecondTen,
  output [3:0] MinuteTen,
  output [3:0] MinuteOne
);

  wire and_1_out, and_2_out, and_3_out, and_4_out, and_5_out, and_6_out, or_1_out, or_2_out, stage3_1_clk,
       stage3_1_resetmain, stage3_1_resetnext, t_ff_1_q, t_ff_2_q, t_ff_3_q, t_ff_4_q, t_ff_5_q, t_ff_6_q,
       t_ff_7_q, t_ff_8_q;

  stage3 stage3_1 (
    .OnOffButton(OnOffButton), .ResetButton(ResetButton), .ST1(SecondTen[0]), .ST2(SecondTen[1]),
    .ST3(SecondTen[2]), .SO1(SecondOne[0]), .SO2(SecondOne[1]), .SO3(SecondOne[2]), .SO4(SecondOne[3]),
    .ResetNext(stage3_1_resetnext), .CLK(stage3_1_clk), .ResetMain(stage3_1_resetmain));
  T_Flip_Flop t_ff_1 (.T(1'b1), .clk(or_2_out), .Q(t_ff_1_q), .reset(or_1_out));  // open: Qn, preset
  D_Flip_Flop d_ff_1 (.D(t_ff_1_q), .clk(stage3_1_clk), .Q(MinuteTen[0]));  // open: Qn, preset, reset
  T_Flip_Flop t_ff_2 (.T(t_ff_1_q), .clk(or_2_out), .Q(t_ff_2_q), .reset(or_1_out));  // open: Qn, preset
  D_Flip_Flop d_ff_2 (.D(t_ff_2_q), .clk(stage3_1_clk), .Q(MinuteTen[1]));  // open: Qn, preset, reset
  and and_1 (and_1_out, t_ff_1_q, t_ff_2_q);
  T_Flip_Flop t_ff_3 (.T(and_1_out), .clk(or_2_out), .Q(t_ff_3_q), .reset(or_1_out));  // open: Qn, preset
  D_Flip_Flop d_ff_3 (.D(t_ff_3_q), .clk(stage3_1_clk), .Q(MinuteTen[2]));  // open: Qn, preset, reset
  and and_2 (and_2_out, and_1_out, t_ff_3_q);
  T_Flip_Flop t_ff_4 (.T(and_2_out), .clk(or_2_out), .Q(t_ff_4_q), .reset(or_1_out));  // open: Qn, preset
  D_Flip_Flop d_ff_4 (.D(t_ff_4_q), .clk(stage3_1_clk), .Q(MinuteTen[3]));  // open: Qn, preset, reset
  and and_3 (and_3_out, t_ff_2_q, t_ff_4_q);
  or or_1 (or_1_out, and_3_out, stage3_1_resetmain);
  T_Flip_Flop t_ff_5 (.T(1'b1), .clk(stage3_1_resetnext), .Q(t_ff_5_q), .reset(or_2_out));  // open: Qn, preset
  D_Flip_Flop d_ff_5 (.D(t_ff_5_q), .clk(stage3_1_clk), .Q(MinuteOne[0]));  // open: Qn, preset, reset
  T_Flip_Flop t_ff_6 (.T(t_ff_5_q), .clk(stage3_1_resetnext), .Q(t_ff_6_q), .reset(or_2_out));  // open: Qn, preset
  D_Flip_Flop d_ff_6 (.D(t_ff_6_q), .clk(stage3_1_clk), .Q(MinuteOne[1]));  // open: Qn, preset, reset
  and and_4 (and_4_out, t_ff_5_q, t_ff_6_q);
  T_Flip_Flop t_ff_7 (.T(and_4_out), .clk(stage3_1_resetnext), .Q(t_ff_7_q), .reset(or_2_out));  // open: Qn, preset
  D_Flip_Flop d_ff_7 (.D(t_ff_7_q), .clk(stage3_1_clk), .Q(MinuteOne[2]));  // open: Qn, preset, reset
  and and_5 (and_5_out, and_4_out, t_ff_7_q);
  T_Flip_Flop t_ff_8 (.T(and_5_out), .clk(stage3_1_resetnext), .Q(t_ff_8_q), .reset(or_2_out));  // open: Qn, preset
  D_Flip_Flop d_ff_8 (.D(t_ff_8_q), .clk(stage3_1_clk), .Q(MinuteOne[3]));  // open: Qn, preset, reset
  and and_6 (and_6_out, t_ff_6_q, t_ff_8_q);
  or or_2 (or_2_out, and_6_out, stage3_1_resetmain);

  assign SecondTen[3] = 1'b0;
endmodule

module stage5 (
  input  Split,
  input  ResetButton
);

  wire and_1_out, and_2_out, and_3_out, and_4_out, and_5_out, and_6_out, and_7_out, and_8_out, and_9_out,
       and_10_out, and_11_out, and_12_out, and_13_out, and_14_out, and_15_out, and_16_out, and_17_out,
       and_18_out, and_19_out, and_20_out, and_21_out, d_ff_1_q, d_ff_4_q, d_ff_7_q, d_ff_9_q, d_ff_14_q,
       d_ff_17_q, d_ff_19_q, d_ff_21_q, nor_1_out, or_1_out, or_2_out, stage3_1_clk, stage3_1_resetmain,
       stage3_1_resetnext, stage3_1_so1, stage3_1_so2, stage3_1_so3, stage3_1_so4, stage3_1_st1,
       stage3_1_st2, stage3_1_st3, t_ff_1_q, t_ff_2_q, t_ff_3_q, t_ff_4_q, t_ff_5_q, t_ff_6_q, t_ff_7_q,
       t_ff_8_q;
  wire [2:0] d_ff_2_q;
  wire [3:0] d_ff_5_q, d_ff_12_q, d_ff_15_q;

  nor nor_1 (nor_1_out, Split, stage3_1_clk);
  stage3 stage3_1 (
    .OnOffButton(1'b1), .ResetButton(ResetButton), .ST1(stage3_1_st1), .ST2(stage3_1_st2),
    .ST3(stage3_1_st3), .SO1(stage3_1_so1), .SO2(stage3_1_so2), .SO3(stage3_1_so3), .SO4(stage3_1_so4),
    .ResetNext(stage3_1_resetnext), .CLK(stage3_1_clk), .ResetMain(stage3_1_resetmain));
  T_Flip_Flop t_ff_1 (.T(1'b1), .clk(or_2_out), .Q(t_ff_1_q), .reset(or_1_out));  // open: Qn, preset
  D_Flip_Flop d_ff_1 (.D(t_ff_1_q), .clk(stage3_1_clk), .Q(d_ff_1_q));  // open: Qn, preset, reset
  and and_1 (and_1_out, 1'b1, stage3_1_st1);
  and and_2 (and_2_out, 1'b1, stage3_1_st2);
  and and_3 (and_3_out, d_ff_1_q, 1'b1);
  D_Flip_Flop d_ff_2 (.D(and_1_out), .clk(nor_1_out), .Q(d_ff_2_q[0]), .reset(stage3_1_resetmain));  // open: Qn, preset
  D_Flip_Flop d_ff_3 (.D(and_2_out), .clk(nor_1_out), .Q(d_ff_2_q[1]), .reset(stage3_1_resetmain));  // open: Qn, preset
  T_Flip_Flop t_ff_2 (.T(t_ff_1_q), .clk(or_2_out), .Q(t_ff_2_q), .reset(or_1_out));  // open: Qn, preset
  D_Flip_Flop d_ff_4 (.D(t_ff_2_q), .clk(stage3_1_clk), .Q(d_ff_4_q));  // open: Qn, preset, reset
  D_Flip_Flop d_ff_5 (.D(and_3_out), .clk(nor_1_out), .Q(d_ff_5_q[0]), .reset(stage3_1_resetmain));  // open: Qn, preset
  and and_4 (and_4_out, t_ff_1_q, t_ff_2_q);
  T_Flip_Flop t_ff_3 (.T(and_4_out), .clk(or_2_out), .Q(t_ff_3_q), .reset(or_1_out));  // open: Qn, preset
  D_Flip_Flop d_ff_6 (.D(and_5_out), .clk(nor_1_out), .Q(d_ff_2_q[2]), .reset(stage3_1_resetmain));  // open: Qn, preset
  and and_5 (and_5_out, 1'b1, stage3_1_st3);
  D_Flip_Flop d_ff_7 (.D(t_ff_3_q), .clk(stage3_1_clk), .Q(d_ff_7_q));  // open: Qn, preset, reset
  and and_6 (and_6_out, d_ff_4_q, 1'b1);
  and and_7 (and_7_out, and_4_out, t_ff_3_q);
  D_Flip_Flop d_ff_8 (.D(and_6_out), .clk(nor_1_out), .Q(d_ff_5_q[1]), .reset(stage3_1_resetmain));  // open: Qn, preset
  Hex_Digit_Display SecondTenSplit (.value({1'b0, d_ff_2_q}));  // open: dp
  T_Flip_Flop t_ff_4 (.T(and_7_out), .clk(or_2_out), .Q(t_ff_4_q), .reset(or_1_out));  // open: Qn, preset
  D_Flip_Flop d_ff_9 (.D(t_ff_4_q), .clk(stage3_1_clk), .Q(d_ff_9_q));  // open: Qn, preset, reset
  and and_8 (and_8_out, t_ff_2_q, t_ff_4_q);
  and and_9 (and_9_out, d_ff_7_q, 1'b1);
  or or_1 (or_1_out, and_8_out, stage3_1_resetmain);
  Hex_Digit_Display hex_digit_display_1 (.value(d_ff_5_q));  // open: dp
  D_Flip_Flop d_ff_10 (
    .D(and_9_out), .clk(nor_1_out), .Q(d_ff_5_q[2]), .reset(stage3_1_resetmain));  // open: Qn, preset
  and and_10 (and_10_out, d_ff_9_q, 1'b1);
  D_Flip_Flop d_ff_11 (
    .D(and_10_out), .clk(nor_1_out), .Q(d_ff_5_q[3]), .reset(stage3_1_resetmain));  // open: Qn, preset
  and and_11 (and_11_out, 1'b1, stage3_1_so1);
  and and_12 (and_12_out, 1'b1, stage3_1_so2);
  D_Flip_Flop d_ff_12 (.D(and_11_out), .clk(nor_1_out), .Q(d_ff_12_q[0]));  // open: Qn, preset, reset
  D_Flip_Flop d_ff_13 (.D(and_12_out), .clk(nor_1_out), .Q(d_ff_12_q[1]));  // open: Qn, preset, reset
  T_Flip_Flop t_ff_5 (.T(1'b1), .clk(stage3_1_resetnext), .Q(t_ff_5_q), .reset(or_2_out));  // open: Qn, preset
  D_Flip_Flop d_ff_14 (.D(t_ff_5_q), .clk(stage3_1_clk), .Q(d_ff_14_q));  // open: Qn, preset, reset
  and and_13 (and_13_out, d_ff_14_q, 1'b1);
  D_Flip_Flop d_ff_15 (
    .D(and_13_out), .clk(nor_1_out), .Q(d_ff_15_q[0]), .reset(stage3_1_resetmain));  // open: Qn, preset
  D_Flip_Flop d_ff_16 (.D(and_14_out), .clk(nor_1_out), .Q(d_ff_12_q[2]));  // open: Qn, preset, reset
  and and_14 (and_14_out, 1'b1, stage3_1_so3);
  T_Flip_Flop t_ff_6 (.T(t_ff_5_q), .clk(stage3_1_resetnext), .Q(t_ff_6_q), .reset(or_2_out));  // open: Qn, preset
  D_Flip_Flop d_ff_17 (.D(t_ff_6_q), .clk(stage3_1_clk), .Q(d_ff_17_q));  // open: Qn, preset, reset
  and and_15 (and_15_out, t_ff_5_q, t_ff_6_q);
  and and_16 (and_16_out, d_ff_17_q, 1'b1);
  T_Flip_Flop t_ff_7 (.T(and_15_out), .clk(stage3_1_resetnext), .Q(t_ff_7_q), .reset(or_2_out));  // open: Qn, preset
  D_Flip_Flop d_ff_18 (.D(and_17_out), .clk(nor_1_out), .Q(d_ff_12_q[3]));  // open: Qn, preset, reset
  and and_17 (and_17_out, 1'b1, stage3_1_so4);
  D_Flip_Flop d_ff_19 (.D(t_ff_7_q), .clk(stage3_1_clk), .Q(d_ff_19_q));  // open: Qn, preset, reset
  D_Flip_Flop d_ff_20 (
    .D(and_16_out), .clk(nor_1_out), .Q(d_ff_15_q[1]), .reset(stage3_1_resetmain));  // open: Qn, preset
  and and_18 (and_18_out, and_15_out, t_ff_7_q);
  T_Flip_Flop t_ff_8 (.T(and_18_out), .clk(stage3_1_resetnext), .Q(t_ff_8_q), .reset(or_2_out));  // open: Qn, preset
  and and_19 (and_19_out, d_ff_19_q, 1'b1);
  Hex_Digit_Display hex_digit_display_2 (.value(d_ff_12_q));  // open: dp
  D_Flip_Flop d_ff_21 (.D(t_ff_8_q), .clk(stage3_1_clk), .Q(d_ff_21_q));  // open: Qn, preset, reset
  D_Flip_Flop d_ff_22 (
    .D(and_19_out), .clk(nor_1_out), .Q(d_ff_15_q[2]), .reset(stage3_1_resetmain));  // open: Qn, preset
  and and_20 (and_20_out, t_ff_6_q, t_ff_8_q);
  or or_2 (or_2_out, and_20_out, stage3_1_resetmain);
  Hex_Digit_Display hex_digit_display_3 (.value(d_ff_15_q));  // open: dp
  and and_21 (and_21_out, d_ff_21_q, 1'b1);
  D_Flip_Flop d_ff_23 (
    .D(and_21_out), .clk(nor_1_out), .Q(d_ff_15_q[3]), .reset(stage3_1_resetmain));  // open: Qn, preset

  // Notes on the sheet:
  //   SecondTenSplit
  //   MinuteOneSplit
  //   SecondOneSplit
  //   MinuteOneSplit
endmodule

module Stage6a (
  input  First,
  input  Second,
  input  Third,
  input  Fourth,
  input  Split,
  input  Reset,
  output FirstOut,
  output SecondOut,
  output ThirdOut,
  output FourthOut
);

  D_Flip_Flop d_ff_1 (.D(First), .clk(Split), .Q(FirstOut), .reset(Reset));  // open: Qn, preset
  D_Flip_Flop d_ff_2 (.D(Second), .clk(Split), .Q(SecondOut), .reset(Reset));  // open: Qn, preset
  D_Flip_Flop d_ff_3 (.D(Third), .clk(Split), .Q(ThirdOut), .reset(Reset));  // open: Qn, preset
  D_Flip_Flop d_ff_4 (.D(Fourth), .clk(Split), .Q(FourthOut), .reset(Reset));  // open: Qn, preset
endmodule

module stage6b (
  input  [3:0] SecondOne,
  input  [3:0] SecondTen,
  input  [3:0] MinuteOne,
  input  [3:0] MinuteTen,
  input  Split,
  input  Reset,
  output [3:0] SecondOneOut,
  output [3:0] SecondTenOut,
  output [3:0] MinuteOneOut,
  output [3:0] MinuteTenOut
);

  Stage6a stage6a_1 (
    .First(SecondOne[0]), .Second(SecondOne[1]), .Third(SecondOne[2]), .Fourth(SecondOne[3]), .Split(Split),
    .Reset(Reset), .FirstOut(SecondOneOut[0]), .SecondOut(SecondOneOut[1]), .ThirdOut(SecondOneOut[2]),
    .FourthOut(SecondOneOut[3]));
  Stage6a stage6a_2 (
    .First(SecondTen[0]), .Second(SecondTen[1]), .Third(SecondTen[2]), .Fourth(SecondTen[3]), .Split(Split),
    .Reset(Reset), .FirstOut(SecondTenOut[0]), .SecondOut(SecondTenOut[1]), .ThirdOut(SecondTenOut[2]),
    .FourthOut(SecondTenOut[3]));
  Stage6a stage6a_3 (
    .First(MinuteOne[0]), .Second(MinuteOne[1]), .Third(MinuteOne[2]), .Fourth(MinuteOne[3]), .Split(Split),
    .Reset(Reset), .FirstOut(MinuteOneOut[0]), .SecondOut(MinuteOneOut[1]), .ThirdOut(MinuteOneOut[2]),
    .FourthOut(MinuteOneOut[3]));
  Stage6a stage6a_4 (
    .First(MinuteTen[0]), .Second(MinuteTen[1]), .Third(MinuteTen[2]), .Fourth(MinuteTen[3]), .Split(Split),
    .Reset(Reset), .FirstOut(MinuteTenOut[0]), .SecondOut(MinuteTenOut[1]), .ThirdOut(MinuteTenOut[2]),
    .FourthOut(MinuteTenOut[3]));
endmodule
