// Logisim project StopWatch-Stage1.circ as structural Verilog: 1 circuit, main circuit stage1
module stage1 (
  input  OnOff,
  output OutStream
);

  T_Flip_Flop t_ff_1 (.T(1'b1), .clk(OnOff), .Q(OutStream));  // open: Qn, reset, preset
endmodule
