// Logisim project StopWatch-Stage2.circ as structural Verilog: 1 circuit, main circuit stage2
module stage2 (
  input  OnOffButton,
  input  ResetButton,
  output SO1,
  output SO2,
  output SO3,
  output SO4,
  output ResetMain,
  output ResetNext,
  output CLK
);

  wire and_1_out, and_3_out, and_4_out, j_k_ff_1_q, j_k_ff_2_q, j_k_ff_3_q, j_k_ff_4_q, or_1_out;

  Clock clock_1 (.out(CLK));
  J_K_Flip_Flop j_k_ff_1 (
    .J(OnOffButton), .K(OnOffButton), .clk(CLK), .Q(j_k_ff_1_q), .reset(or_1_out));  // open: Qn, preset
  D_Flip_Flop d_ff_1 (.D(j_k_ff_1_q), .clk(CLK), .Q(SO1));  // open: Qn, preset, reset
  J_K_Flip_Flop j_k_ff_2 (
    .J(j_k_ff_1_q), .K(j_k_ff_1_q), .clk(CLK), .Q(j_k_ff_2_q), .reset(or_1_out));  // open: Qn, preset
  D_Flip_Flop d_ff_2 (.D(j_k_ff_2_q), .clk(CLK), .Q(SO2));  // open: Qn, preset, reset
  and and_1 (and_1_out, j_k_ff_1_q, j_k_ff_2_q);
  J_K_Flip_Flop j_k_ff_3 (
    .J(and_1_out), .K(and_1_out), .clk(CLK), .Q(j_k_ff_3_q), .reset(or_1_out));  // open: Qn, preset
  D_Flip_Flop d_ff_3 (.D(j_k_ff_3_q), .clk(CLK), .Q(SO3));  // open: Qn, preset, reset
  and and_2 (ResetNext, SO1, SO4);
  and and_3 (and_3_out, and_1_out, j_k_ff_3_q);
  J_K_Flip_Flop j_k_ff_4 (
    .J(and_3_out), .K(and_3_out), .clk(CLK), .Q(j_k_ff_4_q), .reset(or_1_out));  // open: Qn, preset
  D_Flip_Flop d_ff_4 (.D(j_k_ff_4_q), .clk(CLK), .Q(SO4));  // open: Qn, preset, reset
  and and_4 (and_4_out, j_k_ff_2_q, j_k_ff_4_q);
  or or_1 (or_1_out, and_4_out, ResetButton);
  Hex_Digit_Display hex_digit_display_1 (.value({SO4, SO3, SO2, SO1}));  // open: dp

  assign ResetMain = ResetButton;
endmodule
