// Logisim project StopWatch-Stage4.circ as structural Verilog: 4 circuits, main circuit stage1
module stage1 (
  input  OnOff,
  output OutStream
);

  T_Flip_Flop t_ff_1 (.T(1'b1), .clk(OnOff), .Q(OutStream));  // open: Qn, reset, preset
endmodule

module stage2 (
  input  OnOffButton,
  input  ResetButton,
  output SO1,
  output SO2,
  output SO3,
  output SO4,
  output ResetMain,
  output ResetNext,
  output CLK
);

  wire and_1_out, and_3_out, and_4_out, j_k_ff_1_q, j_k_ff_2_q, j_k_ff_3_q, j_k_ff_4_q, or_1_out;

  Clock clock_1 (.out(CLK));
  J_K_Flip_Flop j_k_ff_1 (
    .J(OnOffButton), .K(OnOffButton), .clk(CLK), .Q(j_k_ff_1_q), .reset(or_1_out));  // open: Qn, preset
  D_Flip_Flop d_ff_1 (.D(j_k_ff_1_q), .clk(CLK), .Q(SO1));  // open: Qn, preset, reset
  J_K_Flip_Flop j_k_ff_2 (
    .J(j_k_ff_1_q), .K(j_k_ff_1_q), .clk(CLK), .Q(j_k_ff_2_q), .reset(or_1_out));  // open: Qn, preset
  D_Flip_Flop d_ff_2 (.D(j_k_ff_2_q), .clk(CLK), .Q(SO2));  // open: Qn, preset, reset
  and and_1 (and_1_out, j_k_ff_1_q, j_k_ff_2_q);
  J_K_Flip_Flop j_k_ff_3 (
    .J(and_1_out), .K(and_1_out), .clk(CLK), .Q(j_k_ff_3_q), .reset(or_1_out));  // open: Qn, preset
  D_Flip_Flop d_ff_3 (.D(j_k_ff_3_q), .clk(CLK), .Q(SO3));  // open: Qn, preset, reset
  and and_2 (ResetNext, SO1, SO4);
  and and_3 (and_3_out, and_1_out, j_k_ff_3_q);
  J_K_Flip_Flop j_k_ff_4 (
    .J(and_3_out), .K(and_3_out), .clk(CLK), .Q(j_k_ff_4_q), .reset(or_1_out));  // open: Qn, preset
  D_Flip_Flop d_ff_4 (.D(j_k_ff_4_q), .clk(CLK), .Q(SO4));  // open: Qn, preset, reset
  and and_4 (and_4_out, j_k_ff_2_q, j_k_ff_4_q);
  or or_1 (or_1_out, and_4_out, ResetButton);
  Hex_Digit_Display hex_digit_display_1 (.value({SO4, SO3, SO2, SO1}));  // open: dp

  assign ResetMain = ResetButton;
endmodule

module stage3 (
  input  OnOffButton,
  input  ResetButton,
  output SO1,
  output SO2,
  output SO3,
  output ST1,
  output ST2,
  output ST3,
  output ST4,
  output ResetNext,
  output CLK,
  output ResetMain
);

  wire and_1_out, and_2_out, stage2_1_resetnext, t_ff_1_q, t_ff_2_q, t_ff_3_q;

  T_Flip_Flop t_ff_1 (.T(1'b1), .clk(stage2_1_resetnext), .Q(t_ff_1_q), .reset(ResetNext));  // open: Qn, preset
  D_Flip_Flop d_ff_1 (.D(t_ff_1_q), .clk(CLK), .Q(SO1));  // open: Qn, preset, reset
  T_Flip_Flop t_ff_2 (.T(t_ff_1_q), .clk(stage2_1_resetnext), .Q(t_ff_2_q), .reset(ResetNext));  // open: Qn, preset
  D_Flip_Flop d_ff_2 (.D(t_ff_2_q), .clk(CLK), .Q(SO2));  // open: Qn, preset, reset
  and and_1 (and_1_out, t_ff_1_q, t_ff_2_q);
  T_Flip_Flop t_ff_3 (.T(and_1_out), .clk(stage2_1_resetnext), .Q(t_ff_3_q), .reset(ResetNext));  // open: Qn, preset
  D_Flip_Flop d_ff_3 (.D(t_ff_3_q), .clk(CLK), .Q(SO3));  // open: Qn, preset, reset
  and and_2 (and_2_out, t_ff_2_q, t_ff_3_q);
  stage2 stage2_1 (
    .OnOffButton(OnOffButton), .ResetButton(ResetButton), .SO1(ST1), .SO2(ST2), .SO3(ST3), .SO4(ST4),
    .ResetMain(ResetMain), .ResetNext(stage2_1_resetnext), .CLK(CLK));
  or or_1 (ResetNext, and_2_out, ResetMain);
endmodule

module stage4 (
  input  OnOffButton,
  input  ResetButton,
  output [3:0] SecondOne,
  output [3:0] SecondTen,
  output [3:0] MinuteTen,
  output [3:0] MinuteOne
);

  wire and_1_out, and_2_out, and_3_out, and_4_out, and_5_out, and_6_out, j_k_ff_1_q, j_k_ff_2_q, j_k_ff_3_q,
       j_k_ff_4_q, or_1_out, or_2_out, stage3_1_clk, stage3_1_resetmain, stage3_1_resetnext, t_ff_1_q,
       t_ff_2_q, t_ff_3_q, t_ff_4_q;

  stage3 stage3_1 (
    .OnOffButton(OnOffButton), .ResetButton(ResetButton), .SO1(SecondTen[0]), .SO2(SecondTen[1]),
    .SO3(SecondTen[2]), .ST1(SecondOne[0]), .ST2(SecondOne[1]), .ST3(SecondOne[2]), .ST4(SecondOne[3]),
    .ResetNext(stage3_1_resetnext), .CLK(stage3_1_clk), .ResetMain(stage3_1_resetmain));
  T_Flip_Flop t_ff_1 (.T(1'b1), .clk(or_2_out), .Q(t_ff_1_q), .reset(or_1_out));  // open: Qn, preset
  D_Flip_Flop d_ff_1 (.D(t_ff_1_q), .clk(stage3_1_clk), .Q(MinuteTen[0]));  // open: Qn, preset, reset
  T_Flip_Flop t_ff_2 (.T(t_ff_1_q), .clk(or_2_out), .Q(t_ff_2_q), .reset(or_1_out));  // open: Qn, preset
  D_Flip_Flop d_ff_2 (.D(t_ff_2_q), .clk(stage3_1_clk), .Q(MinuteTen[1]));  // open: Qn, preset, reset
  and and_1 (and_1_out, t_ff_1_q, t_ff_2_q);
  T_Flip_Flop t_ff_3 (.T(and_1_out), .clk(or_2_out), .Q(t_ff_3_q), .reset(or_1_out));  // open: Qn, preset
  D_Flip_Flop d_ff_3 (.D(t_ff_3_q), .clk(stage3_1_clk), .Q(MinuteTen[2]));  // open: Qn, preset, reset
  and and_2 (and_2_out, and_1_out, t_ff_3_q);
  T_Flip_Flop t_ff_4 (.T(and_2_out), .clk(or_2_out), .Q(t_ff_4_q), .reset(or_1_out));  // open: Qn, preset
  D_Flip_Flop d_ff_4 (.D(t_ff_4_q), .clk(stage3_1_clk), .Q(MinuteTen[3]));  // open: Qn, preset, reset
  and and_3 (and_3_out, t_ff_2_q, t_ff_4_q);
  or or_1 (or_1_out, and_3_out, stage3_1_resetmain);
  J_K_Flip_Flop j_k_ff_1 (
    .J(1'b1), .K(1'b1), .clk(stage3_1_resetnext), .Q(j_k_ff_1_q), .reset(or_2_out));  // open: Qn, preset
  D_Flip_Flop d_ff_5 (.D(j_k_ff_1_q), .clk(stage3_1_clk), .Q(MinuteOne[0]));  // open: Qn, preset, reset
  J_K_Flip_Flop j_k_ff_2 (
    .J(j_k_ff_1_q), .K(j_k_ff_1_q), .clk(stage3_1_resetnext), .Q(j_k_ff_2_q), .reset(or_2_out));  // open: Qn, preset
  D_Flip_Flop d_ff_6 (.D(j_k_ff_2_q), .clk(stage3_1_clk), .Q(MinuteOne[1]));  // open: Qn, preset, reset
  and and_4 (and_4_out, j_k_ff_1_q, j_k_ff_2_q);
  J_K_Flip_Flop j_k_ff_3 (
    .J(and_4_out), .K(and_4_out), .clk(stage3_1_resetnext), .Q(j_k_ff_3_q), .reset(or_2_out));  // open: Qn, preset
  D_Flip_Flop d_ff_7 (.D(j_k_ff_3_q), .clk(stage3_1_clk), .Q(MinuteOne[2]));  // open: Qn, preset, reset
  and and_5 (and_5_out, and_4_out, j_k_ff_3_q);
  J_K_Flip_Flop j_k_ff_4 (
    .J(and_5_out), .K(and_5_out), .clk(stage3_1_resetnext), .Q(j_k_ff_4_q), .reset(or_2_out));  // open: Qn, preset
  D_Flip_Flop d_ff_8 (.D(j_k_ff_4_q), .clk(stage3_1_clk), .Q(MinuteOne[3]));  // open: Qn, preset, reset
  and and_6 (and_6_out, j_k_ff_2_q, j_k_ff_4_q);
  or or_2 (or_2_out, and_6_out, stage3_1_resetmain);

  assign SecondTen[3] = 1'b0;
endmodule
