// Logisim project ANDgates.circ as structural Verilog: 1 circuit, main circuit main
module main (
  input  Pin_1,
  input  Pin_2,
  input  Pin_1_2,
  input  Pin_2_2,
  input  Pin_1_3,
  input  Pin_2_3,
  input  Pin_1_4,
  input  Pin_2_4
);

  wire and_1_out, and_2_out, and_3_out, and_4_out;

  and and_1 (and_1_out, Pin_1, Pin_2);
  and and_2 (and_2_out, Pin_1_2, Pin_2_2);
  and and_3 (and_3_out, Pin_1_3, Pin_2_3);
  and and_4 (and_4_out, Pin_1_4, Pin_2_4);
  LED led_1 (.in(and_1_out));
  LED led_2 (.in(and_2_out));
  LED led_3 (.in(and_3_out));
  LED led_4 (.in(and_4_out));

  // Notes on the sheet:
  //   Pin 1 = 0; Pin 2 = 0
  //   Pin 1 = 0; Pin 2 = 1
  //   Pin 1 = 1; Pin 2 = 0
  //   Pin 1 = 1; Pin 2 = 1
endmodule
