// Logisim project Both0or1inputs.circ as structural Verilog: 1 circuit, main circuit main
module main (
  input  in_1,
  input  in_2,
  input  in_3,
  input  in_4,
  input  in_5,
  input  in_6,
  input  in_7,
  input  in_8,
  input  in_9
);

  wire and_1_out, and_2_out, not_1_out, or_1_out, xnor_1_out;

  and and_1 (and_1_out, in_4, in_5, in_6);
  and and_2 (and_2_out, in_7, in_8, in_9);
  NotExactlyOne xnor_1 (.out(xnor_1_out), .in0(in_1), .in1(in_2), .in2(in_3));
  not not_1 (not_1_out, and_2_out);
  LED led_1 (.in(xnor_1_out));
  or or_1 (or_1_out, and_1_out, not_1_out);
  LED led_2 (.in(or_1_out));

  // Notes on the sheet:
  //   First circut
  //   Alternative circut
endmodule
