// Logisim project NOTgates.circ as structural Verilog: 1 circuit, main circuit main
module main (
  input  Pin,
  input  Pin_2
);

  wire not_1_out, not_2_out;

  not not_1 (not_1_out, Pin);
  not not_2 (not_2_out, Pin_2);
  LED led_1 (.in(not_1_out));
  LED led_2 (.in(not_2_out));
endmodule
