// Logisim project XORgates.circ as structural Verilog: 1 circuit, main circuit main
module main (
  input  Pin_1,
  input  Pin_2,
  input  Pin_1_2,
  input  Pin_2_2,
  input  Pin_1_3,
  input  Pin_2_3,
  input  Pin_1_4,
  input  Pin_2_4
);

  wire xor_1_out, xor_2_out, xor_3_out, xor_4_out;

  xor xor_1 (xor_1_out, Pin_1, Pin_2);
  xor xor_2 (xor_2_out, Pin_1_2, Pin_2_2);
  xor xor_3 (xor_3_out, Pin_1_3, Pin_2_3);
  xor xor_4 (xor_4_out, Pin_1_4, Pin_2_4);
  LED led_1 (.in(xor_1_out));
  LED led_2 (.in(xor_2_out));
  LED led_3 (.in(xor_3_out));
  LED led_4 (.in(xor_4_out));
endmodule
