// Logisim project Halfadder and Fulladder.circ as structural Verilog: 1 circuit, main circuit main
module main (
  input  Input_1,
  input  Input_2,
  input  Carry_in,
  input  Input_1_2,
  input  Input_2_2
);

  wire and_1_out, and_2_out, and_3_out, or_1_out, xor_1_out, xor_2_out, xor_3_out;

  xor xor_1 (xor_1_out, Input_1_2, Input_2_2);
  and and_1 (and_1_out, Input_1_2, Input_2_2);
  xor xor_2 (xor_2_out, Input_1, Input_2);
  and and_2 (and_2_out, Input_1, Input_2);
  LED led_1 (.in(and_2_out));
  xor xor_3 (xor_3_out, Carry_in, xor_1_out);
  LED led_2 (.in(xor_2_out));
  and and_3 (and_3_out, Carry_in, xor_1_out);
  or or_1 (or_1_out, and_3_out, and_1_out);
  LED led_3 (.in(xor_3_out));
  LED led_4 (.in(or_1_out));

  // Notes on the sheet:
  //   Half-adder
  //   Full-adder
  //   Carry Output
  //   Sum Output
  //   Sum Output
  //   Carry Output
endmodule
