// Logisim project Stack.circ as structural Verilog: 1 circuit, main circuit main
module main (
  input  Data_in,
  input  Input,
  input  A_B_prime,
  input  Left_Right,
  input  Data_in_left,
  input  Data_in_right,
  input  CLR,
  input  Left_Right_2,
  input  Data_in_left_2,
  input  Data_in_right_2,
  input  CLR_2,
  input  in_12
);

  wire and_1_out, and_2_out, and_3_out, and_4_out, and_5_out, and_6_out, and_7_out, and_8_out, and_9_out,
       and_10_out, and_11_out, and_12_out, and_13_out, and_14_out, and_15_out, and_16_out, and_17_out,
       and_18_out, and_19_out, and_20_out, and_21_out, and_22_out, and_23_out, and_24_out, and_25_out,
       and_26_out, and_27_out, clock_1_out, clock_2_out, clock_3_out, d_ff_1_q, d_ff_2_q, d_ff_3_q, d_ff_4_q,
       d_ff_5_q, d_ff_6_q, d_ff_7_q, d_ff_8_q, d_ff_9_q, d_ff_10_q, d_ff_11_q, d_ff_12_q, d_ff_13_q,
       d_ff_14_q, not_1_out, not_2_out, not_3_out, or_1_out, or_2_out, or_3_out, or_4_out, or_5_out,
       or_6_out, or_7_out, or_8_out, or_9_out, or_10_out;

  Clock clock_1 (.out(clock_1_out));
  Clock clock_2 (.out(clock_2_out));
  not not_1 (not_1_out, A_B_prime);
  and and_1 (and_1_out, Left_Right, Data_in_left);
  Clock clock_3 (.out(clock_3_out));
  D_Flip_Flop d_ff_1 (.D(Data_in), .clk(clock_1_out), .Q(d_ff_1_q));  // open: Qn, preset, reset
  not not_2 (not_2_out, Left_Right);
  and and_2 (and_2_out, not_2_out, d_ff_6_q);
  or or_1 (or_1_out, and_1_out, and_2_out);
  D_Flip_Flop d_ff_2 (.D(or_1_out), .clk(clock_2_out), .Q(d_ff_2_q), .reset(CLR));  // open: Qn, preset
  not not_3 (not_3_out, Left_Right_2);
  and and_3 (and_3_out, Left_Right_2, Data_in_left_2);
  LED led_1 (.in(d_ff_1_q));
  and and_4 (and_4_out, A_B_prime, Input);
  and and_5 (and_5_out, Input, not_1_out);
  LED led_2 (.in(d_ff_2_q));
  and and_6 (and_6_out, not_3_out, d_ff_7_q);
  or or_2 (or_2_out, and_3_out, and_6_out);
  D_Flip_Flop d_ff_3 (.D(or_2_out), .clk(clock_3_out), .Q(d_ff_3_q), .reset(CLR_2));  // open: Qn, preset
  D_Flip_Flop d_ff_4 (.D(d_ff_1_q), .clk(clock_1_out), .Q(d_ff_4_q));  // open: Qn, preset, reset
  LED led_3 (.in(d_ff_4_q));
  LED led_4 (.in(and_4_out));
  LED led_5 (.in(and_5_out));
  and and_7 (and_7_out, Left_Right, d_ff_2_q);
  and and_8 (and_8_out, d_ff_3_q, in_12);
  D_Flip_Flop d_ff_5 (.D(d_ff_4_q), .clk(clock_1_out), .Q(d_ff_5_q));  // open: Qn, preset, reset
  and and_9 (and_9_out, not_2_out, d_ff_9_q);
  or or_3 (or_3_out, and_7_out, and_9_out);
  D_Flip_Flop d_ff_6 (.D(or_3_out), .clk(clock_2_out), .Q(d_ff_6_q), .reset(CLR));  // open: Qn, preset
  and and_10 (and_10_out, Left_Right_2, d_ff_3_q);
  or or_4 (or_4_out, and_10_out, and_11_out);
  LED led_6 (.in(and_8_out));
  LED led_7 (.in(d_ff_5_q));
  LED led_8 (.in(d_ff_6_q));
  and and_11 (and_11_out, not_3_out, d_ff_10_q);
  D_Flip_Flop d_ff_7 (.D(or_4_out), .clk(clock_3_out), .Q(d_ff_7_q), .reset(CLR_2));  // open: Qn, preset
  D_Flip_Flop d_ff_8 (.D(d_ff_5_q), .clk(clock_1_out), .Q(d_ff_8_q));  // open: Qn, preset, reset
  and and_12 (and_12_out, Left_Right, d_ff_6_q);
  LED led_9 (.in(d_ff_8_q));
  and and_13 (and_13_out, not_2_out, d_ff_11_q);
  or or_5 (or_5_out, and_12_out, and_13_out);
  D_Flip_Flop d_ff_9 (.D(or_5_out), .clk(clock_2_out), .Q(d_ff_9_q), .reset(CLR));  // open: Qn, preset
  and and_14 (and_14_out, Left_Right_2, d_ff_7_q);
  or or_6 (or_6_out, and_14_out, and_16_out);
  and and_15 (and_15_out, d_ff_7_q, in_12);
  LED led_10 (.in(and_15_out));
  LED led_11 (.in(d_ff_9_q));
  and and_16 (and_16_out, not_3_out, d_ff_12_q);
  D_Flip_Flop d_ff_10 (.D(or_6_out), .clk(clock_3_out), .Q(d_ff_10_q), .reset(CLR_2));  // open: Qn, preset
  and and_17 (and_17_out, Left_Right, d_ff_9_q);
  or or_7 (or_7_out, and_17_out, and_20_out);
  and and_18 (and_18_out, Left_Right_2, d_ff_10_q);
  and and_19 (and_19_out, d_ff_10_q, in_12);
  LED led_12 (.in(and_19_out));
  and and_20 (and_20_out, not_2_out, d_ff_13_q);
  D_Flip_Flop d_ff_11 (.D(or_7_out), .clk(clock_2_out), .Q(d_ff_11_q), .reset(CLR));  // open: Qn, preset
  LED led_13 (.in(d_ff_11_q));
  and and_21 (and_21_out, not_3_out, d_ff_14_q);
  or or_8 (or_8_out, and_18_out, and_21_out);
  D_Flip_Flop d_ff_12 (.D(or_8_out), .clk(clock_3_out), .Q(d_ff_12_q), .reset(CLR_2));  // open: Qn, preset
  and and_22 (and_22_out, Left_Right, d_ff_11_q);
  or or_9 (or_9_out, and_22_out, and_24_out);
  and and_23 (and_23_out, d_ff_12_q, in_12);
  LED led_14 (.in(and_23_out));
  and and_24 (and_24_out, not_2_out, Data_in_right);
  D_Flip_Flop d_ff_13 (.D(or_9_out), .clk(clock_2_out), .Q(d_ff_13_q), .reset(CLR));  // open: Qn, preset
  and and_25 (and_25_out, Left_Right_2, d_ff_12_q);
  or or_10 (or_10_out, and_25_out, and_26_out);
  D_Flip_Flop d_ff_14 (.D(or_10_out), .clk(clock_3_out), .Q(d_ff_14_q), .reset(CLR_2));  // open: Qn, preset
  LED led_15 (.in(d_ff_13_q));
  and and_26 (and_26_out, not_3_out, Data_in_right_2);
  and and_27 (and_27_out, d_ff_14_q, in_12);
  LED led_16 (.in(and_27_out));

  // Notes on the sheet:
  //   Clock
  //   Clock
  //   Clock
  //   Simple Shift Register
  //   Basic Encoder Circut
  //   A
  //   B
endmodule
